# Fritzing sketch DC Motor PCB (saved by Fritzing 0.9.2b)
circuit board: 2.35091cm x 1.07949cm
breadboards: 1

parts:
  Q1 = TRANSISTOR_NPN [package=to-92]
  D1 = Zener Diode [part_number=1N4732A breakdown_voltage=3.6V package="300 mil [THT]"]
  M1 = DC Motor
  J1 = female pin header, 2 pins [form="♀ (female)"]
  J2 = female pin header, 1 pin [form="♀ (female)"]
  R1 = Resistor [tolerance=±5% resistance=220 package=THT]

nets:
  N1: Q1.E, Q1.C, D1.anode, M1.pin_1, J1.pin1
  N2: Q1.B, R1.Pin_0
  N3: D1.cathode, M1.pin_2, J1.pin2
  N4: J2.pin1, R1.Pin_1

notes:
  -
  +
  in
