# Fritzing sketch DC Motor (saved by Fritzing 0.9.2b)
breadboards: 1

parts:
  M1 = DC Motor
  Q1 = TRANSISTOR_NPN [package=to-92]
  D1 = Zener Diode [part_number=1N4732A breakdown_voltage=3.6V package="300 mil [THT]"]
  Part1 = Arduino Uno (Rev3)
  R1 = Resistor [tolerance=±5% resistance=220 package=THT]

nets:
  N1: M1.pin_1, D1.cathode, Part1.5V
  N2: M1.pin_2, Q1.C, D1.anode
  N3: Q1.E, Part1.GND
  N4: Q1.B, R1.Pin_1
  N5: Part1.D3_PWM, R1.Pin_0
