# Fritzing sketch LCD Temp (saved by Fritzing 0.9.2b)
breadboards: 1

parts:
  Part1 = Arduino Uno (Rev3)
  LCD1 = Adafruit Negative RGB 2x16 LCD
  DHT1 = DHT22 Humidity and Temperature Sensor
  R2 = Trimmer Potentiometer [maximum_resistance=10kΩ package=THT]  # not connected
  R1 = Resistor [tolerance=±5% resistance=220 package="2512 [SMD]"]

nets:
  N1: Part1.D8, R1.Pin_1
  N2: Part1.D11_PWM/MOSI, LCD1.no_name_yet#5
  N3: Part1.D12/MISO, LCD1.no_name_yet#3
  N4: Part1.D2, LCD1.no_name_yet#13
  N5: Part1.D3_PWM, LCD1.no_name_yet#12
  N6: Part1.D4, LCD1.no_name_yet#11
  N7: Part1.D5_PWM, LCD1.no_name_yet#10
  5V: Part1.5V, LCD1.no_name_yet#101, DHT1.VDD
  GND: Part1.GND, LCD1.no_name_yet#100, LCD1.no_name_yet#104, DHT1.GND
  N8: DHT1.DATA, R1.Pin_0

custom parts:
  Adafruit Negative RGB 2x16 LCD: Adafruit Negative 2x16 LCD Display with RGB Backlight
