# Fritzing sketch NEW_DHT22 (saved by Fritzing 0.9.2b)
circuit board: 6.47326cm x 4.45392cm
breadboards: 1

parts:
  Clock1 = Crystal [frequency="16 Mhz" package=THT]
  R9 = Resistor [tolerance=±5% resistance=220 package=THT]
  C7 = Tantalum Capacitor [capacitance=1μF package="200 mil [THT, tantalum]"]
  C8 = Tantalum Capacitor [capacitance=1μF package="200 mil [THT, tantalum]"]
  J8 = Power Jack [package=power_jack_pth]
  POT1 = TRIMPOT [package=3362u-2]
  REG1 = Voltage Regulator [package=to220-igo]
  C9 = Capacitor Polarized [package=cpol-radial-100uf-25v]
  C10 = Capacitor Polarized [package=cpol-radial-100uf-25v]
  IC1 = atmega328 [package=dip]
  J9 = female pin header, 12 pins [form="♀ (female)"]
  DHT2 = DHT22 Humidity and Temperature Sensor

nets:
  N1: Clock1.pin_0, C8.+, IC1.XLAT1
  N2: Clock1.pin_1, C7.+, IC1.XLAT2
  N3: R9.Pin_0, IC1.D8, DHT2.DATA
  N4: R9.Pin_1, J8.PWR, POT1.CCW, DHT2.VDD
  N5: C7.-, C8.-, POT1.CW, IC1.GND#7, DHT2.GND
  N6: REG1.GND, C9.-, C10.-
  N7: REG1.IN, C10.+
  N8: REG1.OUT, C9.+
  N9: IC1.D11_(PWM), J9.pin5
  N10: IC1.D12, J9.pin4
  N11: IC1.GND#21, J9.pin6

notes:
  +
  12
  11
  2
  -
  8
  5
  4
  3
  DB7
  DB6
  DB5
  DB4
  E
  RS
  RW
  V0
  VDD
  VSS
  0
  1
  CLK
  6
  7
  9
  10
  13
