# Fritzing sketch PCB_Layout_New (saved by Fritzing 0.9.2b)
circuit board: 5.23334cm x 4.45181cm
breadboards: 1

parts:
  REG = Voltage Regulator [package=to220-igo]
  C1 = Capacitor Polarized [package=cpol-radial-100uf-25v]
  C2 = Capacitor Polarized [package=cpol-radial-100uf-25v]
  DHT1 = DHT22 Humidity and Temperature Sensor
  POT = TRIMPOT [package=3362u-2]
  R8 = Resistor [tolerance=±5% resistance=220 package=THT]
  C5 = Tantalum Capacitor [capacitance=1μF package="200 mil [THT, tantalum]"]
  C6 = Tantalum Capacitor [capacitance=1μF package="200 mil [THT, tantalum]"]
  J5 = female pin header, 12 pins [form="♀ (female)"]
  Clock = Crystal [frequency="16 Mhz" package=THT]
  J7 = Power Jack [package=power_jack_pth]
  IC = atmega328 [package=dip]

nets:
  GND: REG.GND, C1.-, C2.-, DHT1.GND, POT.CCW, C5.-, C6.-, J5.pin3, J5.pin4, J5.pin11, J7.GND, IC.GND
  N1: REG.IN, C1.+, DHT1.VDD, POT.CW, R8.Pin_1, J7.PWR
  N2: REG.OUT, C2.+, J5.pin2, J5.pin12, IC.AVCC
  N3: DHT1.DATA, R8.Pin_0, IC.D8
  N4: POT.WIPER, J5.pin1
  N5: C5.+, Clock.pin_0, IC.XLAT1
  N6: C6.+, Clock.pin_1, IC.XLAT2
  N7: J5.pin5, IC.D11_(PWM)
  N8: J5.pin6, IC.D12
  N9: J5.pin7, IC.D5_(PWM)
  N10: J5.pin8, IC.D4
  N11: J5.pin9, IC.D3_(PWM)
  N12: J5.pin10, IC.D2

notes:
  VSS
  VDD
  V0
  RS
  RW
  E
  DB4
  DB5
  DB6
  DB7
  3
  4
  5
  +
  -
  VSS, VDD, VO, RS, RW, E, D4, D5, D6, D7, PWR, GND
  8
  11
  12
  GND, PWR, D7, D6, D5, D4, E, RW, RS, VO, VDD, VSS
  2
  CLK
  1
  0
  6
  7
  9
  10
  13
