# Fritzing sketch Mindflex_LEDs (saved by Fritzing 0.9.0b)
breadboards: 1

parts:
  Part1 = Arduino Uno (Rev3)
  LED1 = LED - 5mm [color="Red (633nm)" package="5 mm [THT]"]
  R1 = Resistor [tolerance=±5% resistance=220 package=THT]
  LED2 = LED - 5mm [color="Red (633nm)" package="5 mm [THT]"]
  LED3 = LED - 5mm [color="Red (633nm)" package="5 mm [THT]"]
  R2 = Resistor [tolerance=±5% resistance=220 package=THT]
  R3 = Resistor [tolerance=±5% resistance=220 package=THT]
  U1 = mystery part, 3 pins [chip_label=?]

nets:
  N1: Part1.D11_PWM/MOSI, LED3.anode
  N2: Part1.D12/MISO, LED2.anode
  N3: Part1.D13/SCK, LED1.anode
  N4: Part1.D0/RX, U1.pin1
  N5: Part1.GND, R1.Pin_1, R2.Pin_1, R3.Pin_1, U1.pin3
  N6: LED1.cathode, R1.Pin_0
  N7: LED2.cathode, R2.Pin_0
  N8: LED3.cathode, R3.Pin_0

notes:
  Mindflex EEG Headset.
  Go from the TX of the Mindflex to the RX of the Arduino.
  Gound to ground.s
