# Fritzing sketch Gambit_New (saved by Fritzing 0.9.2b)
breadboards: 1

parts:
  Arduino1 = Arduino Mini (Rev5)
  Part1 = Audio FX Sound Board + 2x2W Amp
  LED3 = smd LED [color="Red (633nm)" package="1206 [SMD]"]
  BATT1 = LiPoly Battery (1300mAh)
  R1 = Resistor [tolerance=±5% resistance=220 package="2512 [SMD]"]
  LED4 = smd LED [color="Red (633nm)" package="1206 [SMD]"]
  LED5 = smd LED [color="Red (633nm)" package="1206 [SMD]"]
  LED6 = smd LED [color="Red (633nm)" package="1206 [SMD]"]
  LED7 = smd LED [color="Red (633nm)" package="1206 [SMD]"]
  LED8 = smd LED [color="Red (633nm)" package="1206 [SMD]"]
  LED9 = smd LED [color="Red (633nm)" package="1206 [SMD]"]
  LED10 = smd LED [color="Red (633nm)" package="1206 [SMD]"]
  LED11 = smd LED [color="Red (633nm)" package="1206 [SMD]"]
  LED12 = smd LED [color="Red (633nm)" package="1206 [SMD]"]
  R2 = Resistor [tolerance=±5% resistance=220 package="2512 [SMD]"]
  R3 = Resistor [tolerance=±5% resistance=220 package="2512 [SMD]"]
  R4 = Resistor [tolerance=±5% resistance=220 package="2512 [SMD]"]
  R5 = Resistor [tolerance=±5% resistance=220 package="2512 [SMD]"]
  R6 = Resistor [tolerance=±5% resistance=220 package="2512 [SMD]"]
  R7 = Resistor [tolerance=±5% resistance=220 package="2512 [SMD]"]
  R8 = Resistor [tolerance=±5% resistance=220 package="2512 [SMD]"]
  R9 = Resistor [tolerance=±5% resistance=220 package="2512 [SMD]"]
  R10 = Resistor [tolerance=±5% resistance=220 package="2512 [SMD]"]
  Pololu_Power_Switch1 = Pololu Power Switch
  SP1 = SPEAKER [package=pcb_mount_speaker]

nets:
  N1: Arduino1.GND, Pololu_Power_Switch1.GND_OUT#5
  N2: Arduino1.5V, Pololu_Power_Switch1.VOUT#7
  N3: Part1.VIN, Pololu_Power_Switch1.VOUT#8
  N4: Part1.GND, Part1.1, Pololu_Power_Switch1.GND_OUT#4
  N5: Part1.R+, SP1.+
  N6: Part1.R-, SP1.-
  N7: LED3.cathode, R1.Pin_1
  N8: BATT1.positive, Pololu_Power_Switch1.VIN
  N9: BATT1.negative, Pololu_Power_Switch1.GND
  N10: R1.Pin_0, R2.Pin_0, R3.Pin_0, R4.Pin_0, R5.Pin_0, R6.Pin_0, R7.Pin_0, R8.Pin_0, R9.Pin_0, R10.Pin_0
  N11: LED4.cathode, R2.Pin_1
  N12: LED5.cathode, R3.Pin_1
  N13: LED6.cathode, R4.Pin_1
  N14: LED7.cathode, R6.Pin_1
  N15: LED8.cathode, R7.Pin_1
  N16: LED9.cathode, R8.Pin_1
  N17: LED10.cathode, R5.Pin_1
  N18: LED11.cathode, R9.Pin_1
  N19: LED12.cathode, R10.Pin_1

custom parts:
  Audio FX Sound Board + 2x2W Amp: The Adafruit Sound Board, the fastest way to add audio effects to a project!
  LiPoly Battery (1300mAh): Lithium Ion Polymer Battery (1300mAh)
  Pololu Power Switch: There are two models of this board. One is LV = 2.5v-7v. The other being SV = 4.5v-20v.
