# Fritzing sketch IR Receiver Sketch (saved by Fritzing 0.8.7b)
breadboards: 1

parts:
  Part1 = Arduino Uno (Rev3)
  DS1 = DS18B20 1-Wire Temperature Sensor [part_number=DS18B20]
  LED1 = LED - 5mm [color="Red (633nm)" package="5 mm [THT]"]

nets:
  N1: Part1.D5_PWM, LED1.anode
  5V: Part1.5V, DS1.VDD
  N2: Part1.GND, DS1.DQ, LED1.cathode

notes:
  IR Receiver
  Left pin: 11
  Middle pin: Ground
  Right pin: Power
