# Fritzing sketch Pot and Servo (saved by Fritzing 0.9.0b)
breadboards: 1

parts:
  Part1 = Arduino Uno (Rev3)
  U2 = POT [package=pot_mammoth]
  J1 = Basic Servo

nets:
  N1: Part1.A0, U2.A
  N2: Part1.D9_PWM, J1.pulse
  5V: Part1.5V, U2.E, J1.vcc
  GND: Part1.GND, U2.S, J1.gnd
