# Fritzing sketch Unltasonic Alarm System (saved by Fritzing 0.9.0b)
breadboards: 1

parts:
  Part1 = Arduino Uno (Rev3)
  LED1 = smd LED [color="Red (633nm)" package="0603 [SMD]"]
  Part2 = SRF05 Ultrasonic Rangefinder
  J1 = Piezo Speaker
  R1 = Resistor [tolerance=±5% resistance=220 package=THT]

nets:
  N1: Part1.D8, Part2.Trig
  N2: Part1.D9_PWM, LED1.anode
  N3: Part1.D5_PWM, J1.pin2
  N4: Part1.D7, Part2.Echo
  5V: Part1.5V, Part2.VCC
  GND: Part1.GND, Part2.GND, J1.pin1, R1.Pin_0
  N5: LED1.cathode, R1.Pin_1
