# Fritzing sketch Record (saved by Fritzing 0.9.2b)
breadboards: 1

parts:
  Part1 = Pro Trinket 3.3V
  R1 = Resistor [tolerance=±5% resistance=220 package=THT]
  R2 = Photocell (LDR) [package=THT]
  NEOPIXEL1 = Neopixel Strip -- White (30/m)

nets:
  GND: Part1.GND, R1.Pin_0, NEOPIXEL1.GND
  +3V3: Part1.+3V3, R2.pin_1, NEOPIXEL1.+5V
  N1: Part1.D6, NEOPIXEL1.Din
  N2: Part1.A0, R1.Pin_1, R2.pin_0

custom parts:
  Pro Trinket 3.3V: The Pro Trinket 3.3V is like an Arduino Pro Mini with more pins and USB included. However, it uses 3V logic and 12MHz clock which means it's good when you want a lower-power and lower-voltage setup. Built with the common core Arduino chip, the ATmega328p, it has 18 GPIO, 2 extra analog inputs, 28K of flash, and 2K of RAM. It has onboard USB bootloading support with Optiboot support, so you can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
  Neopixel Strip -- White (30/m): These NeoPixel strips have 30 digitally-addressable pixel LEDs per meter and are very affordable and are only 12.5 mm wide, 10 mm if you remove the strip from the casing.
